# Fritzing sketch Fritzing_smart_bulb (saved by Fritzing 0.9.3b)
breadboards: 1

parts:
  U1 = NodeMCU V1.0
  KY-1 = Keyes Relay [package=THT]
  Part2 = Lilypad Battery Connect
  LED3 = LEDs [package=led10mm]

nets:
  N1: U1.D1, KY-1.ground
  N2: U1.GND, KY-1.power
  N3: U1.Vin, KY-1.signal
  N4: KY-1.C, Part2.+
  N5: KY-1.NO, LED3.C
  N6: Part2.-, LED3.A

notes:
  IN
  VCC
  240V AC power supply
  D1
  GND
  Vin
  ESP8266
  NodeMCU

custom parts:
  NodeMCU V1.0: ESP9266 based NodeMCU
  Keyes Relay: The Keyes 5V relay module is suitable for SCM development, home appliance control. It uses a 5V~12V TIL control signal which can control DC / AC signal.
  LEDs: LEDs Standard schematic elements and footprints for 5mm, 3mm, 1206, and 0603 sized LEDs. 5mm - Spark Fun Electronics SKU : COM-00529 (and others)
